// Logisim project rgbmatrix1.circ as structural Verilog: 1 circuit, main circuit main
module main (
);

  wire clock_1_out, not_1_out, Reset_out;
  wire [2:0] counter_1_q;
  wire [3:0] counter_1_q_2;
  wire [4:0] adder_1_out, bit_extender_1_out, bit_extender_2_out;
  wire [7:0] shifter_1_out;
  wire [31:0] shifter_2_out;

  Counter #(.width(7), .max('h7f)) counter_1 (
    .load(1'b0), .D({7{1'b0}}), .count(1'b1), .Q({counter_1_q_2, counter_1_q}), .clk(not_1_out),
    .clr(Reset_out));  // open: carry
  not not_1 (not_1_out, clock_1_out);
  Button Reset (.out(Reset_out));
  Clock clock_1 (.out(clock_1_out));
  Shifter shifter_1 (.in(8'h1), .\dist (counter_1_q), .out(shifter_1_out));
  assign bit_extender_1_out = {{2{1'b0}}, counter_1_q};  // Bit_Extender bit_extender_1
  assign bit_extender_2_out = {{1{1'b0}}, counter_1_q_2};  // Bit_Extender bit_extender_2
  Adder #(.width(5)) adder_1 (.a(bit_extender_1_out), .b(bit_extender_2_out), .out(adder_1_out));  // open: cin, cout
  // RGB_Matrix rgb_matrix_1: pin names not known; wires that end beside it: {8{1'b0}}, shifter_2_out[15:8], shifter_2_out[15:8], shifter_1_out
  Shifter #(.width(32)) shifter_2 (.in({32{1'b1}}), .\dist (adder_1_out), .out(shifter_2_out));
endmodule
